// Logisim project SCHEMATIC.circ as structural Verilog
module REGISTER (
  input  [15:0] INPUT,
  input  CLK,
  input  RST,
  output [15:0] OUTPUT
);

  Register #(.width(16)) register_1 (.D(INPUT), .Q(OUTPUT), .clk(CLK), .clr(RST));  // open: en
endmodule

module RAM (
  input  READ,
  input  in_2,
  input  CLK,
  input  RST,
  input  WRITE,
  output out_6
);

  RAM_part #(.dataWidth(16), .bus("separate")) ram_1 (
    .clk(CLK), .ld(WRITE), .clr(RST));  // open: addr, din, data, str, sel
endmodule
